# Fritzing sketch ctrlRGBArduino (saved by Fritzing 0.9.3b)
breadboards: 1

parts:
  U8 = POT [package=pot_mammoth]
  U9 = POT [package=pot_mammoth]
  U10 = POT [package=pot_mammoth]
  Componente2 = Arduino Uno (Rev3)

nets:
  N1: U8.S, U9.S, U10.S, Componente2.5V
  N2: U8.A, Componente2.A2
  N3: U8.E, U9.E, U10.E, Componente2.GND
  N4: U9.A, Componente2.A1
  N5: U10.A, Componente2.A0
