# Fritzing sketch ctrlRGBPico (saved by Fritzing 0.9.3b)
breadboards: 1

parts:
  Mod2 = Raspberry Pi Pico
  U5 = POT [package=pot_mammoth]
  U6 = POT [package=pot_mammoth]
  U7 = POT [package=pot_mammoth]

nets:
  N1: Mod2.pin_3, Mod2.pin_8, Mod2.pin_13, Mod2.pin_18, Mod2.pin_23, Mod2.pin_28, Mod2.pin_33, Mod2.pin_38, U5.E, U6.E, U7.E
  N2: Mod2.pin_31, U7.A
  N3: Mod2.pin_32, U6.A
  N4: Mod2.pin_34, U5.A
  N5: Mod2.pin_36, U5.S, U6.S, U7.S

custom parts:
  Raspberry Pi Pico: Raspberry Pi Pico. Based around the RP2040 microcontroller the Pico is a low cost microcontroller device bringing Raspberry Pi quality, cost, and easy of use to the microcontroller space. Jan 2021, Split part in to two versions: tht (this one) and SMD. This one will drill holes for a .1 in header in pcb to allow plugging in the module as well as providing pads to solder the module to the top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
